# Fritzing sketch esquematico_doggy (saved by Fritzing 0.9.3b)
breadboards: 1

parts:
  A1 = Raspberry Pi 5  # not connected
  U4 = ESP32-38PinWide [part_number=ESP32-38PinWide]
  M4 = Niren can bus module [package=THT]
  U6 = MIC [package=mic_electret_smd]  # not connected
  M6 = RPlidar A1M8 [package=THT]  # not connected
  M7 = gy9250
  Mod1 = Voltage Sensor 25V  # not connected
  Componente1 = Current Sensor 5A  # not connected
  J1 = Basic Force Sensing Resistor (FSR) [package=THT]
  J2 = Basic Servo  # not connected
  J3 = Basic Servo  # not connected
  J4 = Basic Servo  # not connected
  J5 = Basic Servo  # not connected
  J6 = Basic Servo  # not connected
  J7 = Basic Servo  # not connected
  J9 = Basic Servo  # not connected
  J10 = Basic Servo  # not connected
  J11 = Basic Servo  # not connected
  J12 = Basic Servo  # not connected
  J13 = Basic Servo  # not connected
  U7 = SUP500F [package=sup500f]  # not connected
  U8 = GAS_SENSOR [package=mq-3]  # not connected
  VCC1 = 4 x AAA Battery Mount
  VCC2 = 4 x AAA Battery Mount
  U11 = Voltage Regulator [package=sot223]
  IC1 = Rasberry Pi NIOR Camera [chip_label=IC package="DIP (Dual Inline) [THT]"]  # not connected
  IC2 = Rasberry Pi NIOR Camera [chip_label=IC package="DIP (Dual Inline) [THT]"]  # not connected
  J14 = Basic Servo  # not connected
  tft1 = 3.2in tft touch screen  # not connected
  J15 = Basic Force Sensing Resistor (FSR) [package=THT]
  J16 = Basic Force Sensing Resistor (FSR) [package=THT]
  J17 = Basic Force Sensing Resistor (FSR) [package=THT]
  Componente2 = LED Tactile Button Breakout v10 [part_number=BOB-10467]  # not connected
  Mod2 = 2S-BMS  # not connected
  U13 = ESP32-38PinWide [part_number=ESP32-38PinWide]
  M9 = Niren can bus module [package=THT]
  U15 = ESP32-38PinWide [part_number=ESP32-38PinWide]
  M11 = Niren can bus module [package=THT]
  J8 = Basic Servo  # not connected
  R1 = Resistor [tolerance=±5% resistance=220 package="0402 [SMD]"]
  R2 = Resistor [tolerance=±5% resistance=220 package="0402 [SMD]"]
  R3 = Resistor [tolerance=±5% resistance=220 package="0402 [SMD]"]
  R4 = Resistor [tolerance=±5% resistance=220 package="0402 [SMD]"]

nets:
  N1: U4.EN, M4.pin1
  N2: U4.GPIO5, M4.pin3
  N3: U4.GPIO18, M4.pin6
  N4: U4.GPIO19, M4.pin4
  N5: U4.GPIO21, M4.pin7
  N6: U4.GPIO23, M4.pin5
  N7: U4.GND, M4.pin2
  N8: M4.pin8, M4.pin9
  N9: M4.pin12, M9.pin12, M11.pin12
  N10: M4.pin13, M9.pin13, M11.pin13
  N11: M7.pin1, J16.pin_1, U15.VIN
  N12: M7.pin2, U15.GPIO11, R1.Pin_0, R2.Pin_0, R3.Pin_0, R4.Pin_0
  N13: M7.pin4, U15.GPIO22
  N14: J1.pin_0, U15.GPIO36
  N15: VCC1.-, VCC2.-, U11.OUT
  N16: VCC1.+, VCC2.+, U11.ADJ
  N17: J15.pin_0, U15.GPIO39
  N18: J16.pin_0, U15.GPIO35
  N19: J17.pin_0, U15.GPIO34
  N20: U13.EN, M9.pin1
  N21: U13.GPIO5, M9.pin3
  N22: U13.GPIO18, M9.pin6
  N23: U13.GPIO19, M9.pin4
  N24: U13.GPIO21, M9.pin7
  N25: U13.GPIO23, M9.pin5
  N26: U13.GND, M9.pin2
  N27: U15.EN, M11.pin1
  N28: U15.GPIO5, M11.pin3
  N29: U15.GPIO18, M11.pin6
  N30: U15.GPIO19, M11.pin4
  N31: U15.GPIO21, M11.pin7
  N32: U15.GPIO23, M11.pin5
  N33: U15.GND, M11.pin2
  N34: M11.pin8, M11.pin9

notes:
  servo de camara
  microfono
  camara
  paro emergencia
  touch
  maestro
  esclavo final

custom parts:
  Raspberry Pi 5: The RPi5, a faster version of the awesome Raspberry Pi4B ARM Board with 40 pin gpio.
  ESP32-38PinWide: Generic 38-Pin ESP32 with wide format (only access to one side of pins on a breadboard) based on Stephen Lilley's HiLetgo ESP-WROOM-32 ESP32 ESP-32S Development Board.
  Niren can bus module: Niren can bus module availabe on ebay and others. Pcb view assumes that you unsolder the 7 pin header and resolder it on the bottom of the module to connect to the pcb. The two jumpers and the can bus connector remain on the top of the board and don't appear in pcb view.
  RPlidar A1M8: .The RPLIDAR A1 is the next generation low cost 360 degree 2D laser scanner (LIDAR) solution developed by SLAMTEC. It can take up to 4000 samples of laser ranging per second with high rotation speed. And equipped with SLAMTEC patented OPTMAG technology, it breakouts the life limitation of traditional LIDAR system so as to work stably for a long time.
  gy9250: MPU-9250 module (three-axis gyroscope + three-axis acceleration + three-axis magnetic field). The generic model from ebay et. al. rather than the Sparkfun version.
  Rasberry Pi NIOR Camera: Camera
  3.2in tft touch screen: 3.2" tft touch screen lcd display
  2S-BMS: 2S-BMS LIPO battery charger / protection unit. Note pcb does not match the board as it will likely connect with wires, so pcb is 5 pads suitable for .1in header pins.
